// Logisim project 15ComputerBaseChips.circ as structural Verilog: 1 circuit, main circuit main
module main (
  input  In,
  input  a,
  input  b,
  input  a_2,
  input  b_2,
  input  a_3,
  input  b_3,
  input  a_4,
  input  sel,
  input  b_4,
  input  [15:0] in_11,
  input  [15:0] in_12,
  input  sel_3,
  input  in_2,
  input  [15:0] in_15,
  input  [15:0] in_16,
  input  [15:0] in_16_2,
  input  [7:0] in_18,
  input  [15:0] b_16,
  input  sel_4,
  input  in_21,
  input  [15:0] a_16,
  input  in_23,
  input  in_24,
  input  in_25,
  input  in_26,
  input  in_27,
  input  in_28,
  input  in_29,
  input  in_30,
  input  in_31,
  input  in_32,
  input  in_33,
  input  in_34,
  input  in_35,
  input  in_36,
  input  [15:0] a_16_2,
  input  sel_0,
  input  [15:0] in_39,
  input  sel_1,
  input  [15:0] c_16,
  input  in_42,
  input  [15:0] in_43,
  input  [15:0] a_16_3,
  input  [15:0] b_16_2,
  input  sel_0_2,
  input  [15:0] c_16_2,
  input  sel_1_2,
  input  [15:0] d_16,
  input  sel_0_3,
  input  [15:0] e_16,
  input  sel_2,
  input  [15:0] f_16,
  input  sel_0_4,
  input  [15:0] g_16,
  input  sel_1_3,
  input  [15:0] h_16,
  input  sel_0_5,
  input  sel_1_4,
  input  in_3,
  input  cd,
  input  sel_1_5,
  input  sel_0_6,
  input  cd_2,
  input  in_65,
  input  sel_0_7,
  input  efgh,
  input  sel_0_8,
  input  gh,
  input  sel_0_9,
  output [15:0] out_16,
  output [15:0] out_72,
  output [15:0] out_16_2,
  output [15:0] out_16_3,
  output [15:0] out_16_4,
  output [15:0] out_16_5,
  output a_5,
  output b_5,
  output c,
  output d,
  output a_6,
  output b_6,
  output c_2,
  output d_2,
  output e,
  output f,
  output g,
  output h
);

  wire and_1_out, and_4_out, and_5_out, and_7_out, demultiplexer_1_out0, demultiplexer_1_out1,
       demultiplexer_2_out0, demultiplexer_2_out1, demultiplexer_5_out0, demultiplexer_5_out1,
       demultiplexer_6_out0, demultiplexer_6_out1, nand_1_out, nand_2_out, nand_3_out, nand_4_out,
       nand_5_out, nand_6_out, nand_7_out, nand_8_out, not_1_out, not_2_out, not_4_out, not_5_out,
       not_12_out, or_1_out, or_4_out, or_6_out, or_9_out, or_10_out, or_12_out, or_14_out, or_16_out,
       or_19_out, xor_1_out;
  wire [15:0] multiplexer_1_out, multiplexer_2_out, multiplexer_3_out, multiplexer_4_out, multiplexer_5_out,
       multiplexer_6_out, multiplexer_7_out, multiplexer_8_out;

  Demultiplexer demultiplexer_1 (.out0(demultiplexer_1_out0), .out1(demultiplexer_1_out1), .in(in_3), .sel(cd));
  Demultiplexer demultiplexer_2 (.out0(demultiplexer_2_out0), .out1(demultiplexer_2_out1), .in(in_65), .sel(efgh));
  not not_1 (not_1_out, a_2);
  not not_2 (not_2_out, b_2);
  not not_3 (out_16_2[15], in_16_2[15]);
  Multiplexer #(.width(16)) multiplexer_1 (.in0(a_16_3), .in1(b_16_2), .out(multiplexer_1_out), .sel(sel_0_2));
  Multiplexer #(.width(16)) multiplexer_2 (.in0(c_16_2), .in1(d_16), .out(multiplexer_2_out), .sel(sel_0_3));
  Multiplexer #(.width(16)) multiplexer_3 (.in0(e_16), .in1(f_16), .out(multiplexer_3_out), .sel(sel_0_4));
  Multiplexer #(.width(16)) multiplexer_4 (.in0(g_16), .in1(h_16), .out(multiplexer_4_out), .sel(sel_0_5));
  nand nand_1 (nand_1_out, a, b);
  nand nand_2 (nand_2_out, a, b);
  not not_4 (not_4_out, a_3);
  not not_5 (not_5_out, b_3);
  nand nand_3 (nand_3_out, sel, sel);
  nand nand_4 (nand_4_out, sel, b_4);
  not not_6 (out_16_2[13], in_16_2[13]);
  not not_7 (out_16_2[14], in_16_2[14]);
  Multiplexer #(.width(16)) multiplexer_5 (.in0(a_16_2), .in1(in_39), .out(multiplexer_5_out), .sel(sel_0));
  Multiplexer #(.width(16)) multiplexer_6 (.in0(c_16), .in1(in_43), .out(multiplexer_6_out), .sel(in_42));
  Demultiplexer demultiplexer_3 (.out0(a_5), .out1(b_5), .in(demultiplexer_1_out0), .sel(sel_1_4));
  Demultiplexer demultiplexer_4 (.out0(c), .out1(d), .in(demultiplexer_1_out1), .sel(sel_1_5));
  Demultiplexer demultiplexer_5 (
    .out0(demultiplexer_5_out0), .out1(demultiplexer_5_out1), .in(demultiplexer_2_out0), .sel(cd_2));
  Demultiplexer demultiplexer_6 (
    .out0(demultiplexer_6_out0), .out1(demultiplexer_6_out1), .in(demultiplexer_2_out1), .sel(gh));
  nand nand_5 (nand_5_out, In, In);
  LED led_1 (.in(nand_5_out));
  and and_1 (and_1_out, not_1_out, not_2_out);
  and and_2 (out_16[0], in_11[0], in_12[0]);
  or or_1 (or_1_out, sel_3, in_2);
  or or_2 (out_72[0], in_15[0], in_16[0]);
  not not_8 (out_16_2[11], in_16_2[11]);
  not not_9 (out_16_2[12], in_16_2[12]);
  Multiplexer #(.width(16)) multiplexer_7 (
    .in0(multiplexer_1_out), .in1(multiplexer_2_out), .out(multiplexer_7_out), .sel(sel_1_2));
  Multiplexer #(.width(16)) multiplexer_8 (
    .in0(multiplexer_3_out), .in1(multiplexer_4_out), .out(multiplexer_8_out), .sel(sel_1_3));
  nand nand_6 (nand_6_out, nand_1_out, nand_2_out);
  and and_3 (out_16[1], in_11[1], in_12[1]);
  or or_3 (out_72[1], in_15[1], in_16[1]);
  not not_10 (out_16_2[9], in_16_2[9]);
  not not_11 (out_16_2[10], in_16_2[10]);
  or or_4 (or_4_out, in_18[0], in_18[1]);
  Multiplexer #(.width(16)) multiplexer_9 (
    .in0(multiplexer_5_out), .in1(multiplexer_6_out), .out(out_16_4), .sel(sel_1));
  Demultiplexer demultiplexer_7 (.out0(a_6), .out1(b_6), .in(demultiplexer_5_out0), .sel(sel_0_6));
  Demultiplexer demultiplexer_8 (.out0(c_2), .out1(d_2), .in(demultiplexer_5_out1), .sel(sel_0_7));
  Demultiplexer demultiplexer_9 (.out0(e), .out1(f), .in(demultiplexer_6_out0), .sel(sel_0_8));
  Demultiplexer demultiplexer_10 (.out0(g), .out1(h), .in(demultiplexer_6_out1), .sel(sel_0_9));
  LED led_2 (.in(nand_6_out));
  not not_12 (not_12_out, and_1_out);
  LED led_3 (.in(not_12_out));
  and and_4 (and_4_out, a_3, not_5_out);
  and and_5 (and_5_out, not_4_out, b_3);
  nand nand_7 (nand_7_out, a_4, nand_3_out);
  and and_6 (out_16[2], in_11[2], in_12[2]);
  xor xor_1 (xor_1_out, sel_3, or_1_out);
  and and_7 (and_7_out, in_2, sel_3);
  or or_5 (out_72[2], in_15[2], in_16[2]);
  not not_13 (out_16_2[7], in_16_2[7]);
  not not_14 (out_16_2[8], in_16_2[8]);
  or or_6 (or_6_out, or_4_out, in_18[2]);
  Multiplexer multiplexer_10 (.in0(a_16[0]), .in1(b_16[0]), .out(out_16_3[0]), .sel(sel_4));
  Multiplexer multiplexer_11 (.in0(a_16[1]), .in1(b_16[1]), .out(out_16_3[1]), .sel(in_21));
  Multiplexer multiplexer_12 (.in0(a_16[2]), .in1(b_16[2]), .out(out_16_3[2]), .sel(in_23));
  Multiplexer multiplexer_13 (.in0(a_16[3]), .in1(b_16[3]), .out(out_16_3[3]), .sel(in_24));
  Multiplexer multiplexer_14 (.in0(a_16[4]), .in1(b_16[4]), .out(out_16_3[4]), .sel(in_25));
  Multiplexer multiplexer_15 (.in0(a_16[5]), .in1(b_16[5]), .out(out_16_3[5]), .sel(in_26));
  Multiplexer multiplexer_16 (.in0(a_16[6]), .in1(b_16[6]), .out(out_16_3[6]), .sel(in_27));
  Multiplexer multiplexer_17 (.in0(a_16[7]), .in1(b_16[7]), .out(out_16_3[7]), .sel(in_28));
  Multiplexer multiplexer_18 (.in0(a_16[8]), .in1(b_16[8]), .out(out_16_3[8]), .sel(in_29));
  Multiplexer multiplexer_19 (.in0(a_16[9]), .in1(b_16[9]), .out(out_16_3[9]), .sel(in_30));
  Multiplexer multiplexer_20 (.in0(a_16[10]), .in1(b_16[10]), .out(out_16_3[10]), .sel(in_31));
  Multiplexer multiplexer_21 (.in0(a_16[11]), .in1(b_16[11]), .out(out_16_3[11]), .sel(in_32));
  Multiplexer multiplexer_22 (.in0(a_16[12]), .in1(b_16[12]), .out(out_16_3[12]), .sel(in_33));
  Multiplexer multiplexer_23 (.in0(a_16[13]), .in1(b_16[13]), .out(out_16_3[13]), .sel(in_34));
  Multiplexer multiplexer_24 (.in0(a_16[14]), .in1(b_16[14]), .out(out_16_3[14]), .sel(in_35));
  Multiplexer multiplexer_25 (.in0(a_16[15]), .in1(b_16[15]), .out(out_16_3[15]), .sel(in_36));
  and and_8 (out_16[3], in_11[3], in_12[3]);
  or or_7 (out_72[3], in_15[3], in_16[3]);
  not not_15 (out_16_2[5], in_16_2[5]);
  not not_16 (out_16_2[6], in_16_2[6]);
  Multiplexer #(.width(16)) multiplexer_26 (
    .in0(multiplexer_7_out), .in1(multiplexer_8_out), .out(out_16_5), .sel(sel_2));
  and and_9 (out_16[4], in_11[4], in_12[4]);
  LED led_4 (.in(xor_1_out));
  LED led_5 (.in(and_7_out));
  or or_8 (out_72[4], in_15[4], in_16[4]);
  not not_17 (out_16_2[3], in_16_2[3]);
  not not_18 (out_16_2[4], in_16_2[4]);
  or or_9 (or_9_out, or_6_out, in_18[3]);
  or or_10 (or_10_out, and_4_out, and_5_out);
  LED led_6 (.in(or_10_out));
  and and_10 (out_16[5], in_11[5], in_12[5]);
  or or_11 (out_72[5], in_15[5], in_16[5]);
  not not_19 (out_16_2[1], in_16_2[1]);
  not not_20 (out_16_2[2], in_16_2[2]);
  or or_12 (or_12_out, or_9_out, in_18[4]);
  nand nand_8 (nand_8_out, nand_7_out, nand_4_out);
  LED led_7 (.in(nand_8_out));
  and and_11 (out_16[6], in_11[6], in_12[6]);
  or or_13 (out_72[6], in_15[6], in_16[6]);
  not not_21 (out_16_2[0], in_16_2[0]);
  or or_14 (or_14_out, or_12_out, in_18[5]);
  and and_12 (out_16[7], in_11[7], in_12[7]);
  or or_15 (out_72[7], in_15[7], in_16[7]);
  or or_16 (or_16_out, or_14_out, in_18[6]);
  and and_13 (out_16[8], in_11[8], in_12[8]);
  or or_17 (out_72[8], in_15[8], in_16[8]);
  and and_14 (out_16[9], in_11[9], in_12[9]);
  or or_18 (out_72[9], in_15[9], in_16[9]);
  or or_19 (or_19_out, or_16_out, in_18[7]);
  and and_15 (out_16[10], in_11[10], in_12[10]);
  or or_20 (out_72[10], in_15[10], in_16[10]);
  LED led_8 (.in(or_19_out));
  and and_16 (out_16[11], in_11[11], in_12[11]);
  or or_21 (out_72[11], in_15[11], in_16[11]);
  and and_17 (out_16[12], in_11[12], in_12[12]);
  or or_22 (out_72[12], in_15[12], in_16[12]);
  and and_18 (out_16[13], in_11[13], in_12[13]);
  or or_23 (out_72[13], in_15[13], in_16[13]);
  and and_19 (out_16[14], in_11[14], in_12[14]);
  or or_24 (out_72[14], in_15[14], in_16[14]);
  and and_20 (out_16[15], in_11[15], in_12[15]);
  and and_21 (out_16[15], in_11[15], in_12[15]);
  or or_25 (out_72[15], in_15[15], in_16[15]);

  // Other names for the same wires on the sheet: ab0 = out_16_3[0]; ab1 = out_16_3[1]; ab2 = out_16_3[2];
  //   ab3 = out_16_3[3]; ab4 = out_16_3[4]; ab5 = out_16_3[5]; ab6 = out_16_3[6]; ab7 = out_16_3[7];
  //   ab8 = out_16_3[8]; ab9 = out_16_3[9]; ab10 = out_16_3[10]; ab11 = out_16_3[11]; ab12 = out_16_3[12];
  //   ab13 = out_16_3[13]; ab14 = out_16_3[14]; ab15 = out_16_3[15]

  // Notes on the sheet:
  //   OR
  //   MUX
  //   AND16
  //   a[16]
  //   b[16]
  //   DMUX
  //   OR16
  //   a[16]
  //   b[16]
  //   in[8]
  //   b[16]
  //   d[16]
  //   NOT
  //   AND
  //   XOR
  //   NOT16
  //   OR8Way
  //   MUX16
  //   MUX4Way16
  //   MUX8Way16
  //   DMUX4Way
  //   sel[0]
  //   DMUX8Way
  //   sel[2]
  //   aNOT
  //   bNOT
  //   sel[0]
  //   Note: in the MUX8Way16, there are three select bits,
  //   ab
  //   abcd
  //   aNANDb1
  //   aNANDb2
  //   ab[16]
  //   cd[16]
  //   ef[16]
  //   gh[16]
  //   sel[1]
  //   sel[1]
  //   out
  //   bNOT
  //   aNOT
  //   selNANDsel
  //   selNANDb
  //   selORin
  //   ab[16]
  //   cd[16]
  //   in this schematic the least significant select bit (LSSB) is used for lower level decision making.
  //   ab
  //   ef
  //   out
  //   aNOTANDbNOT
  //   abcd[16]
  //   efgh[16]
  //   out
  //   a
  //   b
  //   As the circuit simulates, the higher significant select bits become useful, sel[1] and sel[2], for middle and top level decision making.
  //   aANDbNOT
  //   aNOTANDb
  //   aNANDselNANDsel
  //   out
  //   out
  //   out[16]
endmodule
